# Fritzing sketch LedBrightViaPotentioneter (saved by Fritzing 0.9.0b)
circuit board: 8.46667cm x 5.64444cm
breadboards: 1

parts:
  R1 = Resistor [tolerance=±5% resistance=220 package=THT]
  Part1 = Arduino Uno (Rev3)
  LED1 = LED - 5mm [color="Red (633nm)" package="5 mm [THT]"]
  R2 = Rotary Potentiometer (Small) [maximum_resistance=100kΩ package=THT]

nets:
  N1: R1.Pin_0, Part1.GND, R2.leg1
  N2: R1.Pin_1, LED1.cathode
  N3: Part1.A0, R2.wiper
  N4: Part1.D11_PWM/MOSI, LED1.anode
  N5: Part1.5V, R2.leg2
